# Fritzing sketch LITFit (saved by Fritzing 0.8.7b)

parts:
  Mod1 = seeeduino-xiao
  Part1 = NeoPixel NeoMatrix 8x8 [part_number=1487]
  Part2 = Adafruit DRV2605L [part_number="Adafruit #2305"]
  Part3 = Mono Audio Amp Breakout
  PART1 = Audio Jack (TRRS) 3.5mm Breakout [part_number=BOB-11570]
  U1 = POT [package=3362u]
  Mod2 = seeeduino-xiao
  NEOPIXEL1 = Neopixel Strip -- Black (30/m) [part_number=1376]
  NEOPIXEL2 = Neopixel Strip -- Black (30/m) [part_number=1376]
  SP1 = SPEAKER [package=pcb_mount_speaker]
  SP2 = SPEAKER [package=pcb_mount_speaker]
  MOTOR1 = Vibration Motor
  MOTOR2 = Vibration Motor
  MOTOR3 = Vibration Motor
  MOTOR4 = Vibration Motor
  MOTOR5 = Vibration Motor
  MOTOR6 = Vibration Motor
  U2 = LIPO-2000mAh [package=lipo-2000]  # not connected

nets:
  N1: Mod1.D0, Part3.IN-, PART1.TIP, Mod2.D1
  N2: Mod1.D2, Part1.IN
  N3: Mod1.D5, Part2.SDA
  N4: Mod1.D6, Part2.SCL
  GND: Mod1.GND, Part1.GND, Part2.GND, Part3.GND, PART1.SLEEVE, NEOPIXEL1.GND
  VIN: Mod1.5V, Part1.VDD, Part2.VIN, Part3.VIN, NEOPIXEL1.+5V
  N5: Part2.IN/TRIG, Part3.IN+, PART1.RING1
  N6: Part2.OUT+, MOTOR1.POS, MOTOR2.POS, MOTOR3.POS, MOTOR4.POS, MOTOR5.POS, MOTOR6.POS
  N7: Part2.OUT-, MOTOR1.NEG, MOTOR2.NEG, MOTOR3.NEG, MOTOR4.NEG, MOTOR5.NEG, MOTOR6.NEG
  N8: Part3.OUT+, SP1.-, SP2.-
  N9: Part3.OUT-, SP1.+, SP2.+
  N10: Part3.VOL+, U1.E
  N11: Part3.VOL-, U1.A
  N12: Part3.VOL, U1.S
  N13: Mod2.D2, NEOPIXEL2.Din
  N14: Mod2.D10, NEOPIXEL1.Din
  GND_2: Mod2.GND, NEOPIXEL2.GND
  5V: Mod2.5V, NEOPIXEL2.+5V

notes:
  Left Side Right Side
  Connections are USB-C, so the plug provides power. 5V@2A to Arduino A, 5V@1.2A to arduino B.
  Belt Strip: 48 LEDs
  Jacket Strip: 480 LEDs
  Arduino A
  Arduino B

custom parts:
  seeeduino-xiao: Seeeduino XIAO processor board.
  NeoPixel NeoMatrix 8x8: Put on your sunglasses before wiring up this LED matrix - 64 eye-blistering RGB LEDs adorn the NeoMatrix for a blast of configurable color. Arranged in an 8x8 matrix, each pixel is individually addressable. Only one microcontroller pin is required to control all the LEDs, and you get 24 bit color for each LED.
  Adafruit DRV2605L: The DRV2605 from TI is a fancy little motor driver. Rather than controlling a stepper motor or DC motor, its designed specifically for controlling haptic motors - buzzers and vibration motors. Normally one would just turn those kinds of motors on and off, but this driver has the ability to have various effects when driving a vibe motor. For example, ramping the vibration level up and down,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
  Mono Audio Amp Breakout: Description: This tiny audio amplifier is based on the Texas Instruments TPA2005D1. Its efficient class-D operation means low heat and long battery life. It can drive an 8-Ohm speaker at up to 1.4 Watts; it won't shake a stadium, but it will provide plenty of volume for your audio projects. The fully-differential inputs are safe for floating audio signals such as from our MP3 Shield, and can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
  Audio Jack (TRRS) 3.5mm Breakout: Smartphone audio jack with 4 pins (stereo plus microphone), based on the LUMBERG JEITA RC-5325A TRRS connectors are the audio-style connectors that you see on some phones, MP3 players and development boards. TRRS stands for “Tip, Ring, Ring, Sleeve,” which reflects the fact that, unlike a standard stereo connector, this actually has three conductors and a ground. Some devices use the extra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
  Neopixel Strip -- Black (30/m): These NeoPixel strips have 30 digitally-addressable pixel LEDs per meter and are very affordable and are only 12.5 mm wide, 10 mm if you remove the strip from the casing.
  Vibration Motor: An eccentric vibration motor!
